// Logisim project control_logic.circ as structural Verilog: 1 circuit, main circuit control_logic
module control_logic (
  input  [31:0] inst,
  input  BrEq,
  input  BrLt,
  output PCSel,
  output RegWEn,
  output [2:0] ImmSel,
  output BrUn,
  output ASel,
  output BSel,
  output [3:0] ALUSel,
  output MemRW,
  output [1:0] WBSel,
  output CSRSel,
  output CSRWen
);

  wire alux1x, alux2x, alux3x, alux4x, alux5x, and_1_out, and_2_out, and_3_out, and_4_out, and_15_out,
       and_18_out, and_19_out, and_25_out, B_output, isadd0, isand1, isB13, isB_type, isI_type, isJ_type,
       isJalr_type, isL_type, ismul10, ismulh14, ismulhu11, isor2, isR_type, issll6, isslt7, issra5, issrl4,
       issub12, isU1_type, isU2_type, isxor3, not_1_out, not_2_out, not_3_out, not_4_out, not_5_out,
       not_6_out, not_7_out, not_8_out, not_9_out, not_10_out, not_11_out, not_12_out, not_13_out, or_1_out,
       or_2_out, or_10_out, or_11_out, or_12_out, or_13_out;
  wire [1:0] multiplexer_9_out, multiplexer_10_out, multiplexer_11_out, multiplexer_12_out;
  wire [2:0] multiplexer_1_out, multiplexer_2_out, multiplexer_3_out, multiplexer_4_out, multiplexer_5_out,
       multiplexer_6_out, multiplexer_7_out, multiplexer_8_out;
  wire [3:0] multiplexer_13_out, multiplexer_14_out, multiplexer_15_out, multiplexer_16_out,
       multiplexer_17_out, multiplexer_18_out, multiplexer_19_out, multiplexer_20_out, multiplexer_21_out,
       multiplexer_22_out, multiplexer_23_out, multiplexer_25_out;

  not not_1 (not_1_out, inst[14]);
  not not_2 (not_2_out, inst[12]);
  not not_3 (not_3_out, BrLt);
  not not_4 (not_4_out, BrEq);
  not not_5 (not_5_out, inst[6]);
  not not_6 (not_6_out, inst[5]);
  not not_7 (not_7_out, inst[4]);
  not not_8 (not_8_out, inst[3]);
  not not_9 (not_9_out, inst[2]);
  Multiplexer #(.enable("false"), .width(3)) multiplexer_1 (
    .in0(3'b000), .in1(3'b000), .out(multiplexer_1_out), .sel(isI_type));
  Multiplexer #(.enable("false"), .width(3)) multiplexer_2 (
    .in0(3'b000), .in1(3'b001), .out(multiplexer_2_out), .sel(MemRW));
  Multiplexer #(.enable("false"), .width(3)) multiplexer_3 (
    .in0(3'b000), .in1(3'b010), .out(multiplexer_3_out), .sel(isB_type));
  Multiplexer #(.enable("false"), .width(3)) multiplexer_4 (
    .in0(3'b000), .in1(3'b011), .out(multiplexer_4_out), .sel(isU1_type));
  Multiplexer #(.enable("false"), .width(3)) multiplexer_5 (
    .in0(3'b000), .in1(3'b011), .out(multiplexer_5_out), .sel(isU2_type));
  Multiplexer #(.enable("false"), .width(3)) multiplexer_6 (
    .in0(3'b000), .in1(3'b100), .out(multiplexer_6_out), .sel(isJ_type));
  Multiplexer #(.enable("false"), .width(3)) multiplexer_7 (
    .in0(3'b000), .in1(3'b000), .out(multiplexer_7_out), .sel(isJalr_type));
  Multiplexer #(.enable("false"), .width(3)) multiplexer_8 (
    .in0(3'b000), .in1(3'b101), .out(multiplexer_8_out), .sel(CSRWen));
  and and_1 (and_1_out, not_1_out, not_2_out, not_3_out, BrEq);
  and and_2 (and_2_out, inst[14], inst[12], not_3_out, BrEq);
  and and_3 (and_3_out, inst[14], not_2_out, BrLt, not_4_out);
  and and_4 (and_4_out, not_1_out, inst[12], not_4_out);
  or or_1 (or_1_out, isR_type, isI_type, isU1_type);
  or or_2 (or_2_out, isJalr_type, isJ_type);
  and and_5 (isR_type, not_5_out, inst[5], inst[4], not_8_out, not_9_out);
  and and_6 (isI_type, not_5_out, not_6_out, inst[4], not_8_out, not_9_out);
  and and_7 (isL_type, not_5_out, not_6_out, not_7_out, not_8_out, not_9_out);
  and and_8 (MemRW, not_5_out, inst[5], not_7_out, not_8_out, not_9_out);
  and and_9 (isB_type, inst[6], inst[5], not_7_out, not_8_out, not_9_out);
  and and_10 (isJ_type, inst[6], inst[5], not_7_out, inst[3], inst[2]);
  and and_11 (isJalr_type, inst[6], inst[5], not_7_out, not_8_out, inst[2]);
  and and_12 (isU1_type, not_5_out, not_6_out, inst[4], not_8_out, inst[2]);
  and and_13 (isU2_type, not_5_out, inst[5], inst[4], not_8_out, inst[2]);
  and and_14 (CSRWen, inst[6], inst[5], inst[4], not_8_out, not_9_out);
  and and_15 (and_15_out, isB_type, B_output);
  or or_3 (RegWEn, isR_type, isI_type, isL_type, isJ_type, isJalr_type, isU1_type, isU2_type);
  or or_4 (B_output, and_1_out, and_2_out, and_3_out, and_4_out);
  or or_5 (PCSel, and_15_out, isJ_type, isJalr_type);
  assign ImmSel = multiplexer_1_out | multiplexer_2_out | multiplexer_3_out | multiplexer_4_out | multiplexer_5_out | multiplexer_6_out | multiplexer_7_out | multiplexer_8_out;  // OR_Gate or_6, 3 bits wide
  Multiplexer #(.enable("false"), .width(2)) multiplexer_9 (
    .in0(2'b00), .in1(2'b00), .out(multiplexer_9_out), .sel(or_1_out));
  Multiplexer #(.enable("false"), .width(2)) multiplexer_10 (
    .in0(2'b00), .in1(2'b01), .out(multiplexer_10_out), .sel(or_2_out));
  Multiplexer #(.enable("false"), .width(2)) multiplexer_11 (
    .in0(2'b00), .in1(2'b10), .out(multiplexer_11_out), .sel(isL_type));
  Multiplexer #(.enable("false"), .width(2)) multiplexer_12 (
    .in0(2'b00), .in1(2'b11), .out(multiplexer_12_out), .sel(isU2_type));
  and and_16 (CSRSel, CSRWen, inst[14]);
  assign WBSel = multiplexer_9_out | multiplexer_10_out | multiplexer_11_out | multiplexer_12_out;  // OR_Gate or_7, 2 bits wide
  and and_17 (BrUn, inst[13], isB_type);
  or or_8 (ASel, isB_type, isJ_type, isU1_type);
  or or_9 (BSel, isI_type, isL_type, MemRW, isB_type, isJ_type, isJalr_type, isU1_type, isU2_type);
  not not_10 (not_10_out, alux4x);
  not not_11 (not_11_out, alux3x);
  not not_12 (not_12_out, alux2x);
  not not_13 (not_13_out, alux1x);
  and and_18 (and_18_out, isR_type, alux4x);
  and and_19 (and_19_out, not_11_out, not_12_out, not_13_out);
  and and_20 (isand1, alux3x, alux2x, alux1x);
  and and_21 (isor2, alux3x, alux2x, not_13_out);
  and and_22 (isxor3, alux3x, not_12_out, not_13_out);
  and and_23 (issrl4, alux3x, not_12_out, alux1x);
  and and_24 (issra5, alux4x, alux3x, not_12_out, alux1x);
  and and_25 (and_25_out, not_11_out, not_12_out, alux1x);
  and and_26 (isslt7, not_11_out, alux2x, not_13_out);
  and and_27 (ismulhu11, not_11_out, alux2x, alux1x);
  and and_28 (issub12, and_18_out, not_11_out, not_12_out, not_13_out);
  Demultiplexer #(.enable("false")) demultiplexer_1 (.out0(isadd0), .out1(ismul10), .in(and_19_out), .sel(alux5x));
  Demultiplexer #(.enable("false")) demultiplexer_2 (.out0(issll6), .out1(ismulh14), .in(and_25_out), .sel(alux5x));
  or or_10 (or_10_out, isR_type, isI_type);
  or or_11 (or_11_out, isR_type, isI_type);
  or or_12 (or_12_out, isR_type, isI_type);
  or or_13 (or_13_out, isR_type, isI_type);
  and and_29 (alux2x, inst[13], or_12_out);
  and and_30 (alux4x, inst[30], or_10_out);
  and and_31 (alux3x, inst[14], or_11_out);
  and and_32 (alux1x, inst[12], or_13_out);
  and and_33 (alux5x, inst[25], isR_type);
  Multiplexer #(.enable("false"), .width(4)) multiplexer_13 (
    .in0(4'b0000), .in1(4'b0000), .out(multiplexer_13_out), .sel(isadd0));
  Multiplexer #(.enable("false"), .width(4)) multiplexer_14 (
    .in0(4'b0000), .in1(4'b0001), .out(multiplexer_14_out), .sel(isand1));
  Multiplexer #(.enable("false"), .width(4)) multiplexer_15 (
    .in0(4'b0000), .in1(4'b0010), .out(multiplexer_15_out), .sel(isor2));
  Multiplexer #(.enable("false"), .width(4)) multiplexer_16 (
    .in0(4'b0000), .in1(4'b0011), .out(multiplexer_16_out), .sel(isxor3));
  Multiplexer #(.enable("false"), .width(4)) multiplexer_17 (
    .in0(4'b0000), .in1(4'b0100), .out(multiplexer_17_out), .sel(issrl4));
  Multiplexer #(.enable("false"), .width(4)) multiplexer_18 (
    .in0(4'b0000), .in1(4'b0101), .out(multiplexer_18_out), .sel(issra5));
  Multiplexer #(.enable("false"), .width(4)) multiplexer_19 (
    .in0(4'b0000), .in1(4'b0110), .out(multiplexer_19_out), .sel(issll6));
  Multiplexer #(.enable("false"), .width(4)) multiplexer_20 (
    .in0(4'b0000), .in1(4'b0111), .out(multiplexer_20_out), .sel(isslt7));
  Multiplexer #(.enable("false"), .width(4)) multiplexer_21 (
    .in0(4'b0000), .in1(4'b1010), .out(multiplexer_21_out), .sel(ismul10));
  Multiplexer #(.enable("false"), .width(4)) multiplexer_22 (
    .in0(4'b0000), .in1(4'b1011), .out(multiplexer_22_out), .sel(ismulhu11));
  Multiplexer #(.enable("false"), .width(4)) multiplexer_23 (
    .in0(4'b0000), .in1(4'b1100), .out(multiplexer_23_out), .sel(issub12));
  Multiplexer #(.enable("false"), .width(4)) multiplexer_24 (.in0(4'b0000), .in1(4'b1101), .sel(isB13));  // open: out
  Multiplexer #(.enable("false"), .width(4)) multiplexer_25 (
    .in0(4'b0000), .in1(4'b1110), .out(multiplexer_25_out), .sel(ismulh14));
  assign ALUSel = multiplexer_13_out | multiplexer_14_out | multiplexer_15_out | multiplexer_16_out | multiplexer_17_out | multiplexer_18_out | multiplexer_19_out | multiplexer_20_out | multiplexer_21_out | multiplexer_22_out | multiplexer_23_out | multiplexer_25_out;  // OR_Gate or_14, 4 bits wide

  // Other names for the same wires on the sheet: opcode[6:0] = inst[6:0]; x1 = inst[2]; x2 = inst[3]; x3 = inst[4];
  //   x4 = inst[5]; x5 = inst[6]; alux1 = inst[12]; B = inst[12]; fuct3[2:0] = inst[14:12]; alux2 = inst[13];
  //   A = inst[14]; alux3 = inst[14]; alux5 = inst[25]; fuct7[6:0] = inst[31:25]; alux4 = inst[30];
  //   iscsr_type = CSRWen; isS_type = MemRW

  // Notes on the sheet:
  //   INPUTS to your circuit
  //   DON'T CHANGE THE LOCATIONS OF THE INPUTS AND OUTPUTS!
  //   OUTPUT from your circuit
endmodule
