// Logisim project cpu.circ as structural Verilog: 1 circuit, main circuit cpu
module cpu (
  input  clk,
  input  [31:0] INSTRUCTION,
  input  [31:0] READ_DATA,
  output [31:0] WRITE_ADDRESS,
  output [31:0] PROGRAM_COUNTER,
  output [31:0] ra,
  output [31:0] sp,
  output [31:0] t0,
  output [31:0] t1,
  output [31:0] t2,
  output [31:0] s0,
  output [31:0] s1,
  output [31:0] a0,
  output [31:0] tohost,
  output [3:0] WRITE_ENABLE,
  output [31:0] WRITE_DATA
);

  wire Asel, breq, brlt, brun, Bsel, comparator_1_eq, comparator_2_eq, comparator_3_eq, comparator_4_eq,
       comparator_5_eq, comparator_6_eq, comparator_7_eq, comparator_8_eq, csrsel, csrwen, is_lb_out,
       is_lh_out, is_sb_out, is_sh_out, memrw, pcsel, regfile_1_p7, regfile_1_p8, regfile_1_p10,
       regfile_1_p19, regfile_1_p21, regfile_1_p23, regwe, undriven, undriven_2;
  wire [1:0] wbsel;
  wire [2:0] funct3, immsel;
  wire [3:0] ALUsel, multiplexer_7_out, multiplexer_9_out;
  wire [6:0] funct7;
  wire [24:0] INSTRUCTION_after;
  wire [31:0] adder_1_out, adder_2_out, imm, multiplexer_1_out, multiplexer_2_out, multiplexer_3_out,
       multiplexer_4_out, multiplexer_5_out, multiplexer_8_out, PROGRAM_COUNTER_after, READ_DATA2,
       READ_DATA_8Bits, READ_DATA_16Bits, rs1_data, write_data_t;

  Adder #(.width(32)) adder_1 (.a(PROGRAM_COUNTER), .b(32'h4), .out(adder_1_out));  // open: cin, cout
  Register #(.width(32)) PC (.D(multiplexer_1_out), .en(undriven), .clk(clk), .Q(PROGRAM_COUNTER));  // open: clr
  Multiplexer #(.enable("false"), .width(32)) multiplexer_1 (
    .in0(adder_1_out), .in1(WRITE_ADDRESS), .out(multiplexer_1_out), .sel(pcsel));
  Multiplexer #(.enable("false"), .width(32)) multiplexer_2 (
    .in0(INSTRUCTION), .in1(32'h13), .out(multiplexer_2_out), .sel(pcsel));
  Register #(.width(32)) register_1 (
    .D(multiplexer_2_out), .en(undriven_2), .clk(clk),
    .Q({funct7, INSTRUCTION_after[24:15], funct3, INSTRUCTION_after[11:0]}));  // open: clr
  Register #(.width(32)) register_2 (.D(PROGRAM_COUNTER), .clk(clk), .Q(PROGRAM_COUNTER_after));  // open: en, clr
  control_logic control_logic_1 (
    .CSRWen(csrwen), .PCSel(pcsel), .RegWEn(regwe), .ImmSel(immsel), .BrUn(brun), .ASel(Asel), .BSel(Bsel),
    .ALUSel(ALUsel), .MemRW(memrw), .WBSel(wbsel), .CSRSel(csrsel),
    .inst({funct7, INSTRUCTION_after[24:15], funct3, INSTRUCTION_after[11:0]}), .BrEq(breq), .BrLt(brlt));
  imm_gen imm_gen_1 (
    .inst({funct7, INSTRUCTION_after[24:15], funct3, INSTRUCTION_after[11:0]}), .ImmSel(immsel), .imm(imm));
  // regfile regfile_1: pin names not known; wires that end beside it: INSTRUCTION_after[19:15], INSTRUCTION_after[24:20], INSTRUCTION_after[11:7], write_data_t, regwe, clk, regfile_1_p7, regfile_1_p8, regfile_1_p8, regfile_1_p10, regfile_1_p10, ra, sp, t0, t1, t2, s0, s1, regfile_1_p19, regfile_1_p19, regfile_1_p21, regfile_1_p21, regfile_1_p23
  // branch_comp branch_comp_1: pin names not known; wires that end beside it: rs1_data, WRITE_DATA, brun, a0, rs1_data, WRITE_DATA, breq, brlt
  Multiplexer #(.enable("false"), .width(32)) multiplexer_3 (
    .in0(rs1_data), .in1(PROGRAM_COUNTER_after), .out(multiplexer_3_out), .sel(Asel));
  Multiplexer #(.enable("false"), .width(32)) multiplexer_4 (
    .in0(WRITE_DATA), .in1(imm), .out(multiplexer_4_out), .sel(Bsel));
  Multiplexer #(.enable("false"), .width(32)) multiplexer_5 (
    .in0(rs1_data), .in1(imm), .out(multiplexer_5_out), .sel(csrsel));
  // alu alu_1: pin names not known; wires that end beside it: multiplexer_3_out, multiplexer_4_out, ALUsel, WRITE_ADDRESS
  csr csr_1 (.CSR_address(12'h51e), .CSR_din(multiplexer_5_out), .CSR_WE(csrwen), .clk(clk), .tohost(tohost));
  Adder #(.width(32)) adder_2 (.a(PROGRAM_COUNTER_after), .b(32'h4), .out(adder_2_out));  // open: cin, cout
  Comparator #(.width(7)) comparator_1 (
    .a(INSTRUCTION_after[6:0]), .b(7'b0000011), .eq(comparator_1_eq));  // open: gt, lt
  Comparator #(.width(3)) comparator_2 (.a(funct3), .b(3'b001), .eq(comparator_2_eq));  // open: gt, lt
  Multiplexer #(.enable("false"), .select(2), .width(32)) multiplexer_6 (
    .in0(WRITE_ADDRESS), .in1(adder_2_out), .in2(READ_DATA2), .in3(imm), .out(write_data_t), .sel(wbsel));
  Comparator #(.width(7)) comparator_3 (
    .a(INSTRUCTION_after[6:0]), .b(7'b0100011), .eq(comparator_3_eq));  // open: gt, lt
  and is_sh (is_sh_out, comparator_3_eq, comparator_4_eq);
  Comparator #(.width(3)) comparator_4 (.a(funct3), .b(3'b001), .eq(comparator_4_eq));  // open: gt, lt
  and is_lh (is_lh_out, comparator_1_eq, comparator_2_eq);
  Multiplexer #(.enable("false"), .width(4)) multiplexer_7 (
    .in0(4'b1111), .in1(4'b0011), .out(multiplexer_7_out), .sel(is_sh_out));
  Comparator #(.width(7)) comparator_5 (
    .a(INSTRUCTION_after[6:0]), .b(7'b0100011), .eq(comparator_5_eq));  // open: gt, lt
  Comparator #(.width(3)) comparator_6 (.a(funct3), .b(3'b000), .eq(comparator_6_eq));  // open: gt, lt
  Multiplexer #(.enable("false"), .width(32)) multiplexer_8 (
    .in0(READ_DATA), .in1(READ_DATA_16Bits), .out(multiplexer_8_out), .sel(is_lh_out));
  Multiplexer #(.enable("false"), .width(4)) multiplexer_9 (
    .in0(multiplexer_7_out), .in1(4'b0001), .out(multiplexer_9_out), .sel(is_sb_out));
  and is_sb (is_sb_out, comparator_5_eq, comparator_6_eq);
  assign READ_DATA_8Bits = {{24{READ_DATA[7]}}, READ_DATA[7:0]};  // Bit_Extender bit_extender_1
  assign READ_DATA_16Bits = {{16{READ_DATA[15]}}, READ_DATA[15:0]};  // Bit_Extender bit_extender_2
  Comparator #(.width(7)) comparator_7 (
    .a(INSTRUCTION_after[6:0]), .b(7'b0000011), .eq(comparator_7_eq));  // open: gt, lt
  Comparator #(.width(3)) comparator_8 (.a(funct3), .b(3'b000), .eq(comparator_8_eq));  // open: gt, lt
  Multiplexer #(.enable("false"), .width(4)) multiplexer_10 (
    .in0(4'b0000), .in1(multiplexer_9_out), .out(WRITE_ENABLE), .sel(memrw));
  Multiplexer #(.enable("false"), .width(32)) multiplexer_11 (
    .in0(multiplexer_8_out), .in1(READ_DATA_8Bits), .out(READ_DATA2), .sel(is_lb_out));
  and is_lb (is_lb_out, comparator_7_eq, comparator_8_eq);

  // Other names for the same wires on the sheet: READ_DATA_32Bits[31:0] = READ_DATA; alu1[31:0] = WRITE_ADDRESS;
  //   opcode[6:0] = INSTRUCTION_after[6:0]; rd[4:0] = INSTRUCTION_after[11:7];
  //   INSTRUCTION_after (some bits) = {funct7, funct3}; rs1[4:0] = INSTRUCTION_after[19:15];
  //   rs2[4:0] = INSTRUCTION_after[24:20]; rs2_data[31:0] = WRITE_DATA

  // Notes on the sheet:
  //   Output to IMEM
  //   IMEM (do **NOT** move this)
  //   Inputs from IMEM
  //   It is OK to move the PC, RegFile, ALU, MEM, Branch Comp, Imm Gen, and Control Logic to wherever is most convenient for you when constructing your CPU, and to delete this text
  //   Inputs/Outputs for testing. Do **NOT** move these.
  //   Outputs To DMEM
  //   DMEM (do **NOT** move this)
  //   Inputs From DMEM
endmodule
