// Logisim project imm_gen.circ as structural Verilog: 1 circuit, main circuit imm_gen
module imm_gen (
  input  [31:0] inst,
  input  [2:0] ImmSel,
  output [31:0] imm
);

  wire [31:0] b_typea, csrwi_typea, I_typea, j_typea, s_typea;

  assign I_typea = {{20{inst[31]}}, inst[31:20]};  // Bit_Extender bit_extender_1
  assign s_typea = {{20{inst[31]}}, {inst[31:25], inst[11:7]}};  // Bit_Extender bit_extender_2
  assign csrwi_typea = {{27{1'b0}}, inst[19:15]};  // Bit_Extender bit_extender_3
  assign b_typea = {{19{inst[31]}}, {inst[31], inst[7], inst[30:25], inst[11:8], 1'b0}};  // Bit_Extender bit_extender_4
  assign j_typea = {{11{inst[31]}}, {inst[31], inst[19:12], inst[20], inst[30:21], 1'b0}};  // Bit_Extender bit_extender_5
  Multiplexer #(.enable("false"), .select(3), .width(32)) multiplexer_1 (
    .in0(I_typea), .in1(s_typea), .in2(b_typea), .in3({inst[31:12], {12{1'b0}}}), .in4(j_typea),
    .in5(csrwi_typea), .out(imm), .sel(ImmSel));  // open: in6, in7

  // Other names for the same wires on the sheet: u_typea[31:12] = inst[31:12]

  // Notes on the sheet:
  //   INPUTS to your circuit
  //   DON'T CHANGE THE LOCATIONS OF THE INPUTS AND OUTPUTS!
  //   OUTPUT from your circuit
endmodule
